# Fritzing sketch Smart Locker Circuit Diagram (saved by Fritzing 0.9.3b)

parts:
  Mod1 = Raspberry Pi 4B
  M2 = DC Motor
  S3 = Magnetic Door Switch [package=reed_switch_plastic]
  S4 = Magnetic Door Switch [package=reed_switch_plastic]
  Load_Cell1 = Load Cell - Red/white/black/green
  Load_Cell2 = Load Cell - Red/white/black/green
  USBTTL1 = USB A Plug
  USBTTL2 = Micro USB B Plug
  tft1 = 3.2in tft touch screen  # not connected
  USBTTL3 = Micro USB B Plug
  USBTTL4 = USB A Plug
  2_Channel_Relay1 = 2 Channel Power Relay
  M3 = DC Motor
  J3 = 2.1mm Barrel Jack with Terminal Block
  J4 = Piezo Speaker
  Part1 = HX711 Weighing Sensor Module
  Part2 = HX711 Weighing Sensor Module

nets:
  5V: Mod1.5V, 2_Channel_Relay1.VCC
  GND: Mod1.GND, S3.2, 2_Channel_Relay1.GND
  N1: Mod1.GPIO4, J4.pin2
  N2: Mod1.GPIO23, 2_Channel_Relay1.IN1
  N3: Mod1.GPIO24, 2_Channel_Relay1.IN2
  N4: Mod1.GPIO5, Part1.CK/TX
  N5: Mod1.GPIO6, Part1.DO/RX
  N6: Mod1.GPIO12, S4.1
  N7: Mod1.GPIO19, Part2.DO/RX
  N8: Mod1.GPIO16, S3.1
  N9: Mod1.GPIO26, Part2.CK/TX
  N10: M2.pin_2, 2_Channel_Relay1.K2-NO
  N11: Load_Cell1.wire1, Part1.E+
  N12: Load_Cell1.wire2, Part1.E-
  N13: Load_Cell1.wire3, Part1.A+
  N14: Load_Cell1.wire4, Part1.A-
  N15: Load_Cell2.wire1, Part2.E+
  N16: Load_Cell2.wire2, Part2.E-
  N17: Load_Cell2.wire3, Part2.A+
  N18: Load_Cell2.wire4, Part2.A-
  N19: USBTTL1.usb, USBTTL4.usb
  N20: USBTTL2.usb, USBTTL3.usb
  N21: 2_Channel_Relay1.K1-COM, J3.POS
  N22: 2_Channel_Relay1.K1-NO, M3.pin_2
  N23: M3.pin_1, J3.NEG

notes:
  Raspberry Pi 4
  2 Channel Relay 5V
  7 Inch Touch Screen
  Load Cell 5kg
  Magnetic Door Switch
  Buzzer
  Solenoid Door Lock 12v
  12V Power Supply

custom parts:
  Load Cell - Red/white/black/green: A rectangle load cell/weighting pressure Sensor with four wires - Red, white, black, green. Normally corresponding with E+, E-, A+, A- respectively.
  USB A Plug: USB A Plug breadboard only for documetnation purposes.
  3.2in tft touch screen: 3.2" tft touch screen lcd display
  2 Channel Power Relay: A 2 channel power relay. The module operates at 5V.
